# Fritzing sketch schemaDriver (saved by Fritzing 0.9.0b)

parts:
  Q1 = Basic FET N-Channel [package="TO220 [THT]"]
  R1 = Resistor [tolerance=±5% resistance=10k package=THT]
  R2 = Resistor [tolerance=±5% resistance=4.7k package=THT]
  Q2 = NPN-Transistor [package="TO92 [THT]"]
  C1 = Electrolytic Capacitor [capacitance=1µF package="100 mil [THT, electrolytic]"]
  J1 = Power Jack [package=power_jack_slot]
  J2 = female pin header, 1 pin [form="♀ (female)"]  # not connected
  LED1 = LED - 5mm [color="Red (633nm)" package="5 mm [THT]"]

nets:
  N1: Q1.gate, R1.Pin_1, Q2.C
  N2: Q1.drain, LED1.cathode
  N3: R2.Pin_1, Q2.B
  N4: Q2.E, C1.-, J1.GND
  N5: C1.+, J1.PWR, LED1.anode
